# Fritzing sketch SchemaRFID (saved by Fritzing 0.9.3b)
breadboards: 1

parts:
  Composant1 = RFID-RC522-v2
  J1 = Piezo Speaker
  Grove1 = Grove OLED 128x96
  U2 = NodeMCU V1.0

nets:
  N1: Composant1.SDA, U2.D8
  N2: Composant1.SCK, U2.D5
  N3: Composant1.MOSI, U2.D7
  N4: Composant1.MISO, U2.D6
  GND: Composant1.GND, Grove1.GND, U2.GND#13
  N5: Composant1.RST, U2.D0
  3.3V: Composant1.3.3V, Grove1.VCC, U2.3V3
  N6: J1.pin1, U2.GND#16
  N7: J1.pin2, U2.D4
  N8: Grove1.SDA, U2.D1
  N9: Grove1.SCL, U2.D2

custom parts:
  RFID-RC522-v2: A simple China made RFID-RC522 Reader; do check the pin labels, as this is a MFRC522 based clone.
  NodeMCU V1.0: ESP8266 based NodeMCU V1.0
